# Fritzing sketch neo-controller-buttons (saved by Fritzing 1.0.3b)
breadboards: 1

parts:
  Mod1 = seeeduino-xiao
  S7 = Pushbutton [package="[THT]"]
  S16 = Pushbutton [package="[THT]"]
  S17 = Pushbutton [package="[THT]"]

nets:
  N1: Mod1.D4, S17.Pin_1, S17.Pin_2
  N2: Mod1.D5, S16.Pin_1, S16.Pin_2
  N3: Mod1.D6, S7.Pin_1, S7.Pin_2
  N4: Mod1.GND, S7.Pin_3, S7.Pin_4, S16.Pin_3, S16.Pin_4, S17.Pin_3, S17.Pin_4

notes:
  V-
  5v
  D

custom parts:
  seeeduino-xiao: Seeeduino XIAO processor board.
