# Fritzing sketch neo-controller-rotary (saved by Fritzing 1.0.3b)
breadboards: 1

parts:
  Mod1 = seeeduino-xiao
  CUI-enc1 = Duppa I2C Rotary Encoder

nets:
  N1: Mod1.D3, CUI-enc1.INT
  N2: Mod1.D4, CUI-enc1.SCA
  N3: Mod1.D5, CUI-enc1.SCL
  N4: Mod1.3V3, CUI-enc1.+
  N5: Mod1.GND, CUI-enc1.-

notes:
  V-
  5v
  D

custom parts:
  seeeduino-xiao: Seeeduino XIAO processor board.
  Duppa I2C Rotary Encoder: CUI DuPPa I2C RGB incremental encoder.VCC 5V (3.3V min)
