# Fritzing sketch neo-controller (saved by Fritzing 1.0.3b)
breadboards: 5

parts:
  U1 = Mini-360 DC-DC Buck converter [package=THT]
  Mod1 = seeeduino-xiao
  D1 = Schottky Diode [part_number=1N5817 package="300 mil [THT]"]
  D2 = Schottky Diode [part_number=1N5817 package="300 mil [THT]"]
  Mod3 = seeeduino-xiao
  S7 = Pushbutton [package="[THT]"]
  S8 = Pushbutton [package="[THT]"]
  S9 = Pushbutton [package="[THT]"]
  S10 = Pushbutton [package="[THT]"]
  S11 = Pushbutton [package="[THT]"]
  S12 = Pushbutton [package="[THT]"]
  D4 = Schottky Diode [part_number=1N5817 package="300 mil [THT]"]
  S13 = Pushbutton [package="[THT]"]
  S14 = Pushbutton [package="[THT]"]
  S15 = Pushbutton [package="[THT]"]
  microSD1 = MicroSD Card Module

nets:
  N1: U1.IN+, D1.cathode
  N2: U1.OUT+, D2.anode, D4.anode
  GND: U1.OUT-, Mod1.GND, Mod3.GND, S7.Pin_3, S7.Pin_4, S8.Pin_1, S8.Pin_2, S9.Pin_1, S9.Pin_2, S10.Pin_3, S10.Pin_4, S11.Pin_1, S11.Pin_2, S12.Pin_1, S12.Pin_2, S13.Pin_3, S13.Pin_4, S14.Pin_3, S14.Pin_4, S15.Pin_1, S15.Pin_2, microSD1.GND
  N3: Mod1.D3, microSD1.CS
  N4: Mod1.D6, Mod3.D7
  N5: Mod1.D7, Mod3.D6
  N6: Mod1.D8, microSD1.SCK
  N7: Mod1.D9, microSD1.MISO
  N8: Mod1.D10, microSD1.MOSI
  5V: Mod1.5V, D2.cathode, microSD1.VCC
  N9: Mod3.D0, S7.Pin_1, S7.Pin_2
  N10: Mod3.D1, S10.Pin_1, S10.Pin_2
  N11: Mod3.D2, S11.Pin_3, S11.Pin_4
  N12: Mod3.D3, S12.Pin_3, S12.Pin_4
  N13: Mod3.D4, S9.Pin_3, S9.Pin_4
  N14: Mod3.D5, S8.Pin_3, S8.Pin_4
  N15: Mod3.D8, S13.Pin_1, S13.Pin_2
  N16: Mod3.D9, S14.Pin_1, S14.Pin_2
  N17: Mod3.D10, S15.Pin_3, S15.Pin_4
  N18: Mod3.5V, D4.cathode

notes:
  V-
  V+
  5v
  RX
  D
  TX

custom parts:
  Mini-360 DC-DC Buck converter: Mini-360 DC-DC Buck converter. Tiny buck step down voltage converter, input voltage 4.75 to 23V output 1 to 17V adjustable. Available from ebay and the like.
  seeeduino-xiao: Seeeduino XIAO processor board.
